# Fritzing sketch asi-smart-cooler-diy (saved by Fritzing 1.0.7)
circuit board: 8.46667cm x 5.64444cm
breadboards: 1

parts:
  A1 = Wemos S2-pico
  R1 = Resistor [tolerance=±5% power=0.25W resistance=10k package=THT]
  R2 = Temperature Sensor (Thermistor) [thermistor_type=NTC part_number=B3950 package=THT]
  J2 = Peltier Element [part_number=TEC1-04901]
  J3 = Camdenboss CTB0158-2 [part_number=CTB0158-2 package=THT]
  M1 = xy-mos d4184 [package=THT]
  J4 = XL4015 DC-DC CC CV module (blue)  # not connected

nets:
  N1: A1.Pin_1, R1.Pin_0, R2.pin_1
  N2: A1.Pin_8, A1.Pin_9, R1.Pin_1
  N3: A1.Pin_13, R2.pin_0, J3.pin2, M1.pin2, M1.pin5, M1.pin6, M1.pin7
  N4: A1.Pin_14, J3.pin1, M1.pin8
  N5: A1.Pin_15, M1.pin1, M1.pin4
  N6: J2.pin1, M1.pin9
  N7: J2.pin2, M1.pin10

custom parts:
  Wemos S2-pico: A mini wifi board with OLED based ESP32-S2FN4R2.
  xy-mos d4184: xy-mos d4184 Two parallel N-Channel logic compatible MOSFETS with low Rds(on) for high current low-side switching applications.
  XL4015 DC-DC CC CV module (blue): XL4015 DC-DC CC/CV module blue
